# Fritzing sketch Schema (saved by Fritzing 0.9.3b)
breadboards: 2

parts:
  Q1 = NPN-Transistor [package="TO92 [THT]"]
  M1 = DC Motor
  R2 = Resistor [tolerance=±5% resistance=220 package=THT]
  YL-83_-_Control_Board1 = YL-83 Rain Sensor - Control Board
  YL-83_-_Detection_Board1 = YL-83 Rain Sensor - Detection Board
  DS1 = DS18B20 1-Wire Temperature Sensor Probe Cable
  YL-83_-_Control_Board2 = YL-83 Rain Sensor - Control Board
  YL-83_-_Control_Board3 = YL-83 Rain Sensor - Control Board
  YL-83_-_Control_Board4 = YL-83 Rain Sensor - Control Board
  DS2 = DS18B20 1-Wire Temperature Sensor Probe Cable
  DS3 = DS18B20 1-Wire Temperature Sensor Probe Cable
  Part1 = Arduino Uno (Rev3)
  Q2 = NPN-Transistor [package="TO92 [THT]"]
  Q3 = NPN-Transistor [package="TO92 [THT]"]
  Q4 = NPN-Transistor [package="TO92 [THT]"]
  R3 = Resistor [tolerance=±5% resistance=220 package=THT]
  R4 = Resistor [tolerance=±5% resistance=220 package=THT]
  R5 = Resistor [tolerance=±5% resistance=220 package=THT]
  M2 = DC Motor
  M3 = DC Motor
  M4 = DC Motor

nets:
  N1: Q1.E, Part1.VIN, Q2.E, Q3.E, Q4.E
  N2: Q1.B, R2.Pin_0
  N3: Q1.C, M1.pin_2
  GND: M1.pin_1, DS1.GND, DS2.GND, DS3.GND, Part1.GND, M2.pin_1, M3.pin_1, M4.pin_1
  N4: R2.Pin_1, Part1.D11_PWM/MOSI
  VCC: YL-83_-_Control_Board1.VCC, DS1.VDD, YL-83_-_Control_Board2.VCC, YL-83_-_Control_Board3.VCC, YL-83_-_Control_Board4.VCC, DS2.VDD, DS3.VDD, Part1.5V
  N5: YL-83_-_Control_Board1.GND, Part1.D10_PWM/SS
  N6: YL-83_-_Control_Board1.DO, Part1.D2
  N7: YL-83_-_Control_Board1.POS, YL-83_-_Detection_Board1.POS
  N8: YL-83_-_Control_Board1.NEG, YL-83_-_Detection_Board1.NEG
  N9: DS1.shield, DS2.shield, DS3.shield, Part1.D8
  N10: YL-83_-_Control_Board2.GND, Part1.D7
  N11: YL-83_-_Control_Board2.AO, Part1.A0
  N12: YL-83_-_Control_Board3.GND, Part1.D6_PWM
  N13: YL-83_-_Control_Board3.AO, Part1.A1
  N14: YL-83_-_Control_Board4.GND, Part1.D4
  N15: YL-83_-_Control_Board4.AO, Part1.A2
  N16: Part1.D9_PWM, R4.Pin_1
  N17: Part1.D12/MISO, R3.Pin_1
  N18: Part1.D5_PWM, R5.Pin_1
  N19: Q2.B, R3.Pin_0
  N20: Q2.C, M2.pin_2
  N21: Q3.B, R4.Pin_0
  N22: Q3.C, M3.pin_2
  N23: Q4.B, R5.Pin_0
  N24: Q4.C, M4.pin_2

custom parts:
  YL-83 Rain Sensor - Control Board: The YL-83 is a rain sensor that has more resistance when dry and less resistance when wet. The module runs at 5V.
  YL-83 Rain Sensor - Detection Board: The YL-83 is a rain sensor that has more resistance when dry and less resistance when wet. The module runs at 5V.
